// Logisim project lifestyle.circ as structural Verilog: 1 circuit
module main (
);

  wire A0_p1, A1_p1, A2_p1, A3_p1, adder_1_p10, B0_p1, B1_p1, B2_p1, B3_p1, constant_1_p1, notgate_1_p2,
       notgate_2_p2, notgate_3_p2, notgate_4_p2, notgate_5_p2;

  // InputPin A0: pin names not known; wires that end beside it: A0_p1
  // InputPin A1: pin names not known; wires that end beside it: A1_p1
  // InputPin A2: pin names not known; wires that end beside it: A2_p1
  // InputPin A3: pin names not known; wires that end beside it: A3_p1
  // InputPin B0: pin names not known; wires that end beside it: B0_p1
  // InputPin B1: pin names not known; wires that end beside it: B1_p1
  // InputPin B2: pin names not known; wires that end beside it: B2_p1
  // InputPin B3: pin names not known; wires that end beside it: B3_p1
  // NotGate notgate_1: pin names not known; wires that end beside it: B0_p1, notgate_1_p2
  // NotGate notgate_2: pin names not known; wires that end beside it: B1_p1, notgate_2_p2
  // NotGate notgate_3: pin names not known; wires that end beside it: B2_p1, notgate_3_p2
  // NotGate notgate_4: pin names not known; wires that end beside it: B3_p1, notgate_4_p2
  // Constant constant_1: pin names not known; wires that end beside it: constant_1_p1
  // Adder adder_1: pin names not known; wires that end beside it: constant_1_p1, A0_p1, A1_p1, A2_p1, A3_p1, notgate_1_p2, notgate_2_p2, notgate_3_p2, notgate_4_p2, adder_1_p10
  // NotGate notgate_5: pin names not known; wires that end beside it: adder_1_p10, notgate_5_p2
  // OutputPin S0: pin names not known
  // OutputPin S1: pin names not known
  // OutputPin S2: pin names not known
  // OutputPin S3: pin names not known
  // OutputPin BORROW_OUT: pin names not known; wires that end beside it: notgate_5_p2
endmodule
